# Fritzing sketch Montagem (saved by Fritzing 0.9.3b)

parts:
  Componente1 = Arduino Uno (Rev3)
  J4 = Basic Servo
  J5 = Basic Servo
  PWM1 = PCA9685 16x12-bit PWM Breakout
  J6 = Basic Servo
  J7 = Basic Servo
  Power_plug1 = Power plug

nets:
  N1: Componente1.A4/SDA, PWM1.no_name_yet#504
  N2: Componente1.A5/SCL, PWM1.no_name_yet#503
  N3: Componente1.5V, PWM1.no_name_yet#505
  GND: Componente1.GND, J4.gnd, J5.gnd, PWM1.no_name_yet#501, PWM1.no_name_yet#701, PWM1.no_name_yet#1000, PWM1.no_name_yet#1001, PWM1.no_name_yet#1002, PWM1.no_name_yet#1003, J6.gnd, J7.gnd, Power_plug1.GND
  VCC: J4.vcc, J5.vcc, PWM1.no_name_yet#100, PWM1.no_name_yet#101, PWM1.no_name_yet#102, PWM1.no_name_yet#103, PWM1.no_name_yet#706, J6.vcc, J7.vcc, Power_plug1.VCC
  N4: J4.pulse, PWM1.no_name_yet#3
  N5: J5.pulse, PWM1.no_name_yet#1
  N6: PWM1.no_name_yet#0, J7.pulse
  N7: PWM1.no_name_yet#2, J6.pulse
